# Fritzing sketch Sabouri-Milad-assignment-2 (saved by Fritzing 0.9.3b)
breadboards: 2

parts:
  J1 = Basic Force Sensing Resistor (FSR) [package=THT]
  Part1 = Arduino Uno (Rev3)
  J2 = Basic Force Sensing Resistor (FSR) [package=THT]
  J3 = Basic Force Sensing Resistor (FSR) [package=THT]
  J4 = Basic Force Sensing Resistor (FSR) [package=THT]
  S1 = Pushbutton [package="[THT]"]
  LED1 = LED - 5mm [color="Red (633nm)" package="5 mm [THT]"]
  LED2 = LED - 5mm [color="Green (560nm)" package="5 mm [THT]"]
  LED3 = LED - 5mm [color="Yellow (595nm)" package="5 mm [THT]"]
  LED4 = LED - 5mm [color="Blue (505nm)" package="5 mm [THT]"]
  R1 = Resistor [tolerance=±5% resistance=10k package=THT]
  R2 = Resistor [tolerance=±5% resistance=10k package=THT]
  R3 = Resistor [tolerance=±5% resistance=10k package=THT]
  R4 = Resistor [tolerance=±5% resistance=10k package=THT]
  J6 = Piezo Speaker
  R6 = Resistor [tolerance=±5% resistance=220 package=THT]
  R7 = Resistor [tolerance=±5% resistance=220 package=THT]
  R8 = Resistor [tolerance=±5% resistance=220 package=THT]
  R9 = Resistor [tolerance=±5% resistance=220 package=THT]
  R10 = Resistor [tolerance=±5% resistance=100k package=THT]
  LCD1 = LCD screen
  R11 = Resistor [tolerance=±5% resistance=220 package=THT]
  R12 = Rotary Potentiometer (Small) [maximum_resistance=100kΩ package=THT]

nets:
  N1: J1.pin_0, Part1.A0, R4.Pin_1
  5V: J1.pin_1, Part1.5V, J2.pin_1, J3.pin_1, J4.pin_1, S1.Pin_1, S1.Pin_2, J6.pin2, LCD1.VDD, LCD1.LED+, R12.leg2
  N2: Part1.A1, J2.pin_0, R2.Pin_1
  N3: Part1.A2, J3.pin_0, R1.Pin_1
  N4: Part1.A3, J4.pin_0, R3.Pin_1
  GND: Part1.A4/SDA, Part1.GND, LED1.cathode, LED2.cathode, LED3.cathode, LED4.cathode, R1.Pin_0, R2.Pin_0, R3.Pin_0, R4.Pin_0, R10.Pin_0, LCD1.VSS, LCD1.R/W, R11.Pin_0, R12.leg1
  N5: Part1.D8, LCD1.E
  N6: Part1.D9_PWM, LCD1.DB4
  N7: Part1.D10_PWM/SS, LCD1.DB5
  N8: Part1.D11_PWM/MOSI, LCD1.DB6
  N9: Part1.D12/MISO, LCD1.DB7
  N10: Part1.D2, R6.Pin_0
  N11: Part1.D3_PWM, R7.Pin_0
  N12: Part1.D4, R8.Pin_0
  N13: Part1.D5_PWM, R9.Pin_0
  N14: Part1.D6_PWM, J6.pin1
  N15: Part1.D7, LCD1.RS
  N16: S1.Pin_3, S1.Pin_4, R10.Pin_1
  N17: LED1.anode, R6.Pin_1
  N18: LED2.anode, R7.Pin_1
  N19: LED3.anode, R8.Pin_1
  N20: LED4.anode, R9.Pin_1
  N21: LCD1.V0, R12.wiper
  N22: LCD1.LED-, R11.Pin_1
