# Fritzing sketch MiladSabouri_Assig3-4 (saved by Fritzing 0.9.3b)
breadboards: 1

parts:
  Part1 = Arduino Board Ethernet
  Part2 = Arduino Uno (Rev3)  # not connected
  R1 = Resistor [tolerance=±5% resistance=220 package=THT]
  Part6 = Adafruit Bluefruit LE UART Friend [part_number="Adafruit #2479"]

nets:
  N1: Part1.D8, Part6.RTS
  N2: Part1.D9_PWM, Part6.RXI
  N3: Part1.D11/MOSI, Part6.CTS
  N4: Part1.A0, R1.Pin_1
  N5: Part1.D2_PWM, Part6.TXO
  N6: Part1.D5_PWM, Part6.MODE
  5V: Part1.5V, Part6.VIN
  GND: Part1.GND, R1.Pin_0, Part6.GND

notes:
  To Probe
  Milad Sabouri
  Embedded Systems
  Assignments 3 & 4
  Spring 2018

custom parts:
  Adafruit Bluefruit LE UART Friend: The Bluefruit LE UART Friend makes it easy to add Bluetooth Low Energy connectivity to anything with a hardware or software serial port. We even have nice hardware flow control so you won't have to think about losing data. Connect to your Arduino or other microcontroller or even just a standard FTDI cable for debugging and testing.
