# Fritzing sketch FinalProject_MiladSabouri (saved by Fritzing 0.9.3b)
breadboards: 1

parts:
  Part1 = Arduino Ethernet Shield (Rev3)
  Part2 = Arduino Uno (Rev3) - ICSP  # not connected
  Part4 = Adafruit Bluefruit LE UART Friend [part_number="Adafruit #2479"]
  DHT1 = DHT22 Humidity and Temperature Sensor
  S1 = Pushbutton [package="[THT]"]
  Part7 = 14-segment LED Alphanumeric Backpack [part_number=1911]

nets:
  N1: Part1.D8, Part4.RTS
  N2: Part1.PWM_D9, Part4.RXI
  N3: Part1.PWM_D11, Part4.CTS
  N4: Part1.A0, S1.Pin_3, S1.Pin_4
  N5: Part1.A4/SDA, Part7.SDA
  N6: Part1.A5/SCL, Part7.SCL
  N7: Part1.D2, Part4.TXO
  N8: Part1.PWM_D5, Part4.MODE
  N9: Part1.PWM_D6, DHT1.DATA
  VDD: Part1.5V, Part4.VIN, DHT1.VDD, Part7.VDD, Part7.VI2C
  GND: Part1.GND, Part4.GND, DHT1.GND, S1.Pin_1, S1.Pin_2, Part7.GND

notes:
  Final Project
  ITMT 593 - Embedded Systems
  Milad Sabouri

custom parts:
  Adafruit Bluefruit LE UART Friend: The Bluefruit LE UART Friend makes it easy to add Bluetooth Low Energy connectivity to anything with a hardware or software serial port. We even have nice hardware flow control so you won't have to think about losing data. Connect to your Arduino or other microcontroller or even just a standard FTDI cable for debugging and testing.
  14-segment LED Alphanumeric Backpack: This is a nice, bright alphanumeric display that shows letters and numbers. It's super bright and designed for viewing from distances up to 23 feet (7 meters) away. Four digits with 14 segments on a black surface and we give you a set of two alphanumeric displays as well as a driver board so you can make a clock or a four letter word. Like our other LED backpacks, these are end-to-end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
